// Digital circuit projeto_sem1.dig as structural Verilog
module projeto_sem1 (
  input  clock,
  output [3:0] db__estado,
  output [3:0] db__jogada
);

  wire reset_out, u_fluxo_dados_fim_contagem, u_fluxo_dados_fim_tempo, u_fluxo_dados_jogada_feita,
       u_fluxo_dados_perdeu, u_fluxo_dados_start_pulso, u_unidade_controle_conta_timer,
       u_unidade_controle_limpar, u_unidade_controle_registrar, u_unidade_controle_zera_timer;
  wire [4:0] botao_4__start_out;

  Button reset (.out(reset_out));
  unidade_controle #(.applicationType("IVERILOG")) u_unidade_controle (
    .clock(clock), .start(u_fluxo_dados_start_pulso), .fim_contagem(u_fluxo_dados_fim_contagem),
    .fim_tempo(u_fluxo_dados_fim_tempo), .perdeu(u_fluxo_dados_perdeu), .jogada(u_fluxo_dados_jogada_feita),
    .reset(reset_out), .limpaR(u_unidade_controle_limpar), .registraR(u_unidade_controle_registrar),
    .zera_timer(u_unidade_controle_zera_timer), .conta_timer(u_unidade_controle_conta_timer),
    .db_estado(db__estado));
  Button botao_0 (.out(botao_4__start_out[0]));
  Button botao_1 (.out(botao_4__start_out[1]));
  Button botao_2 (.out(botao_4__start_out[2]));
  Button botao_3 (.out(botao_4__start_out[3]));
  Button botao_4__start (.out(botao_4__start_out[4]));
  fluxo_dados #(.applicationType("IVERILOG")) u_fluxo_dados (
    .clock(clock), .botoes_raw(botao_4__start_out), .limpaR(u_unidade_controle_limpar),
    .registraR(u_unidade_controle_registrar), .zera_timer(u_unidade_controle_zera_timer),
    .conta_timer(u_unidade_controle_conta_timer), .db_estado(db__estado), .reset(reset_out),
    .start_pulso(u_fluxo_dados_start_pulso), .fim_contagem(u_fluxo_dados_fim_contagem),
    .fim_tempo(u_fluxo_dados_fim_tempo), .perdeu(u_fluxo_dados_perdeu),
    .jogada_feita(u_fluxo_dados_jogada_feita), .s_jogada(db__jogada));
  Seven_Seg_Hex seven_seg_hex_1 (.d(db__estado), .dp(1'b0));
  Seven_Seg_Hex seven_seg_hex_2 (.d(db__jogada), .dp(1'b0));

  // Notes on the sheet:
  //   clock: Hz: 1000
endmodule

/* Code of unidade_controle:
module unidade_controle (
    input clock,
    input reset,
    input start,               // start_pulso do FD
    input jogada,              // Vem do jogada_feita do FD
    input fim_contagem,        // Sinal do FD indicando fim do 3-2-1      
    input fim_tempo,           // Sinal do FD indicando fim da música/sessão      
    input perdeu,              // Sinal do FD indicando limite de erros atingido         
    output reg registraR,      // Sinal para o FD salvar a jogada
    output reg limpaR,         // Sinal para o FD limpar o registrador
    output reg zera_timer,
    output reg conta_timer,
    output reg [3:0] db_estado // Depuração nos displays
);

    parameter idle      = 4'b0000; // 0: Aguardando START
    parameter countdown = 4'b0001; // 1: Preparação 3, 2, 1
    parameter play      = 4'b0010; // 2: Execução do jogo
    parameter pause     = 4'b0011; // 3: Jogo pausado
    parameter end_win   = 4'b0100; // 4: Vitoria
    parameter end_lose  = 4'b0101; // 5: Derrota

    reg [3:0] Eatual, Eprox;

    always @(posedge clock or posedge reset) begin
        if (reset) Eatual <= idle;
        else Eatual <= Eprox;
    end

    always @* begin
        case (Eatual)
            idle:      Eprox = start ? countdown : idle;
            countdown: Eprox = fim_contagem ? play : countdown;
            play:      Eprox = perdeu ? end_lose : 
                               (fim_tempo ? end_win : 
                               (start ? pause : play));
            pause:     Eprox = start ? play : pause;
            end_win:   Eprox = start ? idle : end_win;
            end_lose:  Eprox = start ? idle : end_lose;
            default:   Eprox = idle;
        endcase
    end

    always @* begin
        zera_timer  = (Eatual == idle || Eatual == end_win || Eatual == end_lose) ? 1'b1 : 1'b0;
        conta_timer = (Eatual == countdown || Eatual == play) ? 1'b1 : 1'b0;
        limpaR      = (Eatual == idle) ? 1'b1 : 1'b0;
        registraR   = (Eatual == play && jogada) ? 1'b1 : 1'b0;
        db_estado   = Eatual;
    end

endmodule
*/

/* Code of fluxo_dados:
module fluxo_dados (
    input clock,
    input reset,
    
    // Sinais de controle vindos da UC para gerenciar a jogada
    input limpaR,              
    input registraR,           
    input zera_timer,        
    input conta_timer,         
    input [3:0] db_estado, 
    
    // Entradas fisicas
    input [4:0] botoes_raw,    // [4] = Start/Pause, [3:0] = Botoes do jogo
    
    // Saidas de dados e controle
    output [3:0] s_jogada,     // Jogada
    output jogada_feita,       // Indica aperto de nota
    output start_pulso,        // Indica aperto do start
    
    output fim_contagem,
    output fim_tempo,
    output perdeu
);

    // Separando os botões para facilitar a logica
    wire [3:0] botoes_trilha = botoes_raw[3:0]; // Botoes do jogo
    wire start = botoes_raw[4];                 // Botao de controle

    // Verifica se ha jogada
    wire s_tem_jogada = |botoes_trilha; 

    // Gera o pulso de 'jogada_feita' para avisar a UC
    edge_detector u_edge_jogada (
        .clock(clock),
        .reset(reset | limpaR),
        .sinal(s_tem_jogada),
        .pulso(jogada_feita)
    );

    // Temporizador de 3 segundos para o countdown
    contador_m #(.M(3000), .N(12)) timer_countdown (
        .clock   (clock),
        .zera_as (reset),
        .zera_s  (zera_timer),
        // Conta apenas quando a UC autoriza e estamos no estado COUNTDOWN (0001)
        .conta   (conta_timer && (db_estado == 4'b0001)),
        .Q       (),             
        .fim     (fim_contagem), // Gera o sinal que faz a UC pular para PLAY
        .meio    ()
    );

    // Registrador que "salva" a jogada quando a UC manda (registraR)
    registrador_4 RegBotoes (
        .clock(clock),
        .clear(limpaR),
        .enable(registraR),
        .D(botoes_trilha),
        .Q(s_jogada)
    );

    // Detector de borda para o Start/Pause
    edge_detector u_edge_start (
        .clock(clock),
        .reset(reset),
        .sinal(start),
        .pulso(start_pulso)
    );

    // Sinais temporarios
	assign fim_tempo = botoes_raw[0] & botoes_raw[1]; 
	assign perdeu    = botoes_raw[2] & botoes_raw[3];

endmodule

module edge_detector (
    input  clock,
    input  reset,
    input  sinal,
    output pulso
);

    reg reg0;
    reg reg1;

    always @(posedge clock or posedge reset) begin
        if (reset) begin
            reg0 <= 1'b0;
            reg1 <= 1'b0;
        end else if (clock) begin
            reg0 <= sinal;
            reg1 <= reg0;
        end
    end

    assign pulso = ~reg1 & reg0;

endmodule

module registrador_4 (
    input        clock,
    input        clear,
    input        enable,
    input  [3:0] D,
    output [3:0] Q
);

    reg [3:0] IQ;

    always @(posedge clock or posedge clear) begin
        if (clear)
            IQ <= 0;
        else if (enable)
            IQ <= D;
    end

    assign Q = IQ;

endmodule

module contador_m #(parameter M=100, N=7)
  (
   input  wire          clock,
   input  wire          zera_as,
   input  wire          zera_s,
   input  wire          conta,
   output reg  [N-1:0]  Q,
   output reg           fim,
   output reg           meio
  );

  always @(posedge clock or posedge zera_as) begin
    if (zera_as) begin
      Q <= 0;
    end else if (clock) begin
      if (zera_s) begin
        Q <= 0;
      end else if (conta) begin
        if (Q == M-1) begin
          Q <= 0;
        end else begin
          Q <= Q + 1'b1;
        end
      end
    end
  end

  // Saidas
  always @ (Q)
      if (Q == M-1)   fim = 1;
      else            fim = 0;

  always @ (Q)
      if (Q == M/2-1) meio = 1;
      else            meio = 0;

endmodule
*/
